// Logisim project BIRD_castellano.circ as structural Verilog: 3 circuits, main circuit Procesador_BIRD
module Procesador_BIRD (
  input  [15:0] PCi_STOP_addr,
  input  Clk_auto_tick_enabled
);

  wire A_BEQ, A_LDX, A_OP, A_OPI, A_STX, add, addi, and_1_out, and_bis, andi, beq, bge, bgt, ble, bls, bne,
       BUSQ1, BUSQ2, call, clk, clock_1_out, comparator_1_eq, comparator_1_gt, CSal, decoder_1_out21,
       decoder_1_out22, decoder_1_out23, decoder_1_out24, decoder_1_out25, decoder_1_out26, decoder_1_out27,
       decoder_1_out28, decoder_1_out29, decoder_1_out30, decoder_1_out31, decoder_3_out10, decoder_3_out11,
       decoder_3_out12, decoder_3_out13, decoder_3_out14, decoder_3_out15, decoder_3_out16, decoder_3_out17,
       decoder_3_out18, decoder_3_out19, decoder_3_out20, decoder_3_out21, decoder_3_out22, decoder_3_out23,
       decoder_3_out24, decoder_3_out25, decoder_3_out26, decoder_3_out27, decoder_3_out28, decoder_3_out29,
       decoder_3_out30, decoder_3_out31, Desc, div, divi, E_OP, E_OPI, E_PC, in_bis, jmp, L_BEQ, L_LDX, L_OP,
       L_OPI, L_ST, L_STX, ld, LD_BR, LD_IR1, LD_IR2, LD_o1, LD_o2, LD_PC, LD_PCi, LD_ual, ldd, ldx, M_E_LD,
       M_E_LDX, M_ST, M_STX, MCS, MOE, mov, mova, movi, mul, muli, multiplexer_6_out, MWR, nor_1_out,
       not_1_out, not_2_out, or_bis, ori, out_bis, outm, outrm, outs, pop, push, reset_PC, ret, retm, sD,
       sDatM, sES, shl, shr, st, std, step_once, stx, sub, subi, VE, xnor_1_out, xor_bis, xori, Z;
  wire [1:0] sDirM;
  wire [3:0] Cod_UAL;
  wire [4:0] ESnc, estado, multiplexer_5_out, multiplexer_7_out, rd_rf2, rf1, rf2, tabla_saltos_data;
  wire [5:0] CO;
  wire [7:4] senales_de_control;
  wire [15:0] adder_1_out, BR_q1, BR_q2, controlled_buffer_1_out, MEM_dout, multiplexer_1_out,
       multiplexer_2_out, multiplexer_3_out, multiplexer_4_out, multiplexer_8_out, PC, PCi, R_o1_q, R_o2_q,
       ual_1_y, VAR_plus_rf;
  wire [15:5] VAR_i_despl;

  LED led_1 (.in(ld));
  LED led_2 (.in(st));
  LED led_3 (.in(mov));
  LED led_4 (.in(add));
  LED led_5 (.in(sub));
  LED led_6 (.in(mul));
  LED led_7 (.in(div));
  LED led_8 (.in(and_bis));
  LED led_9 (.in(or_bis));
  LED led_10 (.in(xor_bis));
  Multiplexer #(.width(16)) multiplexer_1 (.in0(PC), .in1(PCi), .out(multiplexer_1_out), .sel(sD));
  Multiplexer #(.width(16)) multiplexer_2 (.in0(16'h1), .in1({VAR_i_despl, rf2}), .out(multiplexer_2_out), .sel(sD));
  LED led_11 (.in(L_OP));
  LED led_12 (.in(A_OP));
  LED led_13 (.in(E_OP));
  // Probe on CO
  LED led_14 (.in(ldx));
  LED led_15 (.in(stx));
  LED led_16 (.in(movi));
  LED led_17 (.in(addi));
  LED led_18 (.in(subi));
  LED led_19 (.in(muli));
  LED led_20 (.in(divi));
  LED led_21 (.in(andi));
  LED led_22 (.in(ori));
  LED led_23 (.in(xori));
  LED led_24 (.in(beq));
  Adder #(.width(16)) adder_1 (.a(multiplexer_1_out), .b(multiplexer_2_out), .out(adder_1_out));  // open: cin, cout
  LED led_25 (.in(L_OPI));
  LED led_26 (.in(A_OPI));
  LED led_27 (.in(E_OPI));
  // Probe on clk
  Decoder #(.enable("false"), .select(5)) decoder_1 (
    .out0(BUSQ1), .out1(BUSQ2), .out2(Desc), .out3(L_OP), .out4(A_OP), .out5(E_OP), .out6(L_OPI),
    .out7(A_OPI), .out8(E_OPI), .out9(M_E_LD), .out10(L_ST), .out11(M_ST), .out12(L_LDX), .out13(A_LDX),
    .out14(M_E_LDX), .out15(L_STX), .out16(A_STX), .out17(M_STX), .out18(L_BEQ), .out19(A_BEQ), .out20(E_PC),
    .out21(decoder_1_out21), .out22(decoder_1_out22), .out23(decoder_1_out23), .out24(decoder_1_out24),
    .out25(decoder_1_out25), .out26(decoder_1_out26), .out27(decoder_1_out27), .out28(decoder_1_out28),
    .out29(decoder_1_out29), .out30(decoder_1_out30), .out31(decoder_1_out31), .sel(estado));
  Register #(.width(16)) u_PC (.D(adder_1_out), .en(LD_PC), .clk(clk), .Q(PC), .clr(reset_PC));
  // Probe on adder_1_out
  // Probe on {VAR_i_despl, rf2}
  LED led_28 (.in(M_E_LD));
  // Probe on CO
  // Probe on CO
  // Probe on CO
  // Probe on CO
  // Probe on CO
  // Probe on PC
  // Probe on VAR_plus_rf
  LED led_29 (.in(BUSQ1));
  LED led_30 (.in(BUSQ2));
  LED led_31 (.in(Desc));
  // Probe on CO
  LED led_32 (.in(L_ST));
  LED led_33 (.in(M_ST));
  // Probe on rd_rf2
  // Probe on rd_rf2
  // Probe on rd_rf2
  // Probe on rd_rf2
  Register #(.width(16)) u_PCi (.D(PC), .en(LD_PCi), .clk(clk), .Q(PCi), .clr(reset_PC));
  Multiplexer #(.select(2), .width(16)) multiplexer_3 (
    .in0(PC), .in1(VAR_plus_rf), .in2({VAR_i_despl, rf2}), .out(multiplexer_3_out), .sel(sDirM));  // open: in3
  LED led_34 (.in(L_LDX));
  LED led_35 (.in(A_LDX));
  LED led_36 (.in(M_E_LDX));
  // Probe on rf1
  // Probe on rf1
  // Probe on rf1
  // Probe on rf1
  RAM #(.addrWidth(16), .asyncread("true"), .dataWidth(16), .\type ("nonvolatile")) MEM (
    .addr(multiplexer_3_out), .we(MWR), .oe(MOE), .clk(clk), .din(R_o2_q), .dout(MEM_dout));
  // Probe on multiplexer_3_out
  // Probe on R_o2_q
  LED led_37 (.in(L_STX));
  LED led_38 (.in(A_STX));
  LED led_39 (.in(M_STX));
  // Probe on VAR_i_despl[15:8]
  // Probe on VAR_i_despl[15:8]
  // Probe on VAR_i_despl[15:8]
  LED led_40 (.in(L_BEQ));
  LED led_41 (.in(A_BEQ));
  LED led_42 (.in(Z));
  LED led_43 (.in(E_PC));
  // Probe on {VAR_i_despl[7:5], rf2}
  // Probe on rf2
  // Probe on {VAR_i_despl[7:5], rf2}
  // Probe on {VAR_i_despl[7:5], rf2}
  assign controlled_buffer_1_out = MCS ? MEM_dout : 16'bz;  // Controlled_Buffer controlled_buffer_1
  // Probe on controlled_buffer_1_out
  Register #(.width(16)) IR1 (.D(controlled_buffer_1_out), .en(LD_IR1), .clk(clk), .Q({CO, rd_rf2, rf1}));  // open: clr
  Register #(.width(16)) IR2 (
    .D(controlled_buffer_1_out), .en(LD_IR2), .clk(clk), .Q({VAR_i_despl, rf2}));  // open: clr
  // Probe on {VAR_i_despl, rf2}
  // Probe on rf1
  // Probe on rd_rf2
  // Probe on CO
  // Probe on VAR_plus_rf
  Multiplexer #(.width(16)) multiplexer_4 (
    .in0(VAR_plus_rf), .in1(controlled_buffer_1_out), .out(multiplexer_4_out), .sel(sDatM));
  // Probe on rf2
  not not_1 (not_1_out, CO[5]);
  Decoder #(.select(5)) decoder_2 (
    .out0(ld), .out1(ldd), .out2(ldx), .out3(st), .out4(std), .out5(stx), .out6(mova), .out7(mov),
    .out8(movi), .out9(add), .out10(addi), .out11(sub), .out12(subi), .out13(mul), .out14(muli), .out15(div),
    .out16(divi), .out17(shr), .out18(shl), .out19(and_bis), .out20(andi), .out21(or_bis), .out22(ori),
    .out23(xor_bis), .out24(xori), .out25(jmp), .out26(beq), .out27(bne), .out28(bls), .out29(ble),
    .out30(bgt), .out31(bge), .sel(CO[4:0]), .en(not_1_out));
  Decoder #(.select(5)) decoder_3 (
    .out0(retm), .out1(call), .out2(ret), .out3(push), .out4(pop), .out5(in_bis), .out6(out_bis),
    .out7(outs), .out8(outm), .out9(outrm), .out10(decoder_3_out10), .out11(decoder_3_out11),
    .out12(decoder_3_out12), .out13(decoder_3_out13), .out14(decoder_3_out14), .out15(decoder_3_out15),
    .out16(decoder_3_out16), .out17(decoder_3_out17), .out18(decoder_3_out18), .out19(decoder_3_out19),
    .out20(decoder_3_out20), .out21(decoder_3_out21), .out22(decoder_3_out22), .out23(decoder_3_out23),
    .out24(decoder_3_out24), .out25(decoder_3_out25), .out26(decoder_3_out26), .out27(decoder_3_out27),
    .out28(decoder_3_out28), .out29(decoder_3_out29), .out30(decoder_3_out30), .out31(decoder_3_out31),
    .sel(CO[4:0]), .en(CO[5]));
  Button u_Reset_PC (.out(reset_PC));
  Button u_Step_once (.out(step_once));
  Multiplexer #(.width(5)) multiplexer_5 (
    .in0(rf2), .in1(rd_rf2), .out(multiplexer_5_out), .sel(senales_de_control[7]));
  ROM #(.addrWidth(6), .dataWidth(5)) tabla_saltos (.addr(CO), .data(tabla_saltos_data));
  ROM #(.addrWidth(6), .dataWidth(4)) ROM_UAL (.addr(CO), .data(Cod_UAL));
  Multiplexer multiplexer_6 (.in0(Z), .in1(1'b1), .out(multiplexer_6_out), .sel(VE));
  xnor xnor_1 (xnor_1_out, multiplexer_6_out, CSal);
  Banco_de_Registros BR (
    .LD_BR(LD_BR), .DAT(multiplexer_4_out), .rf2(multiplexer_5_out), .rf1(rf1), .rd(rd_rf2), .clk(clk),
    .Q1(BR_q1), .Q2(BR_q2));
  Counter #(.max('h1f), .width(5)) Contador_de_estado (
    .load(xnor_1_out), .up(1'b1), .count(not_2_out), .clk(clk), .D(multiplexer_7_out), .Q(estado));  // open: clr, carry
  not not_2 (not_2_out, xnor_1_out);
  Multiplexer #(.width(5)) multiplexer_7 (.in0(ESnc), .in1(tabla_saltos_data), .out(multiplexer_7_out), .sel(sES));
  Comparator #(.mode("unsigned"), .width(16)) comparator_1 (
    .a(PCi), .b(PCi_STOP_addr), .gt(comparator_1_gt), .eq(comparator_1_eq));  // open: lt
  Register #(.width(16)) R_o1 (.D(BR_q1), .en(LD_o1), .clk(clk), .Q(R_o1_q));  // open: clr
  // Probe on BR_q1
  Register #(.width(16)) R_o2 (.D(BR_q2), .en(LD_o2), .clk(clk), .Q(R_o2_q));  // open: clr
  // Probe on BR_q2
  // Digital_Oscilloscope #(.nState(5)) digital_oscilloscope_1: pin names not known; wires that end beside it: clk
  Clock clock_1 (.out(clock_1_out));
  nor nor_1 (nor_1_out, comparator_1_gt, comparator_1_eq);
  and and_1 (and_1_out, clock_1_out, nor_1_out, Clk_auto_tick_enabled);
  Multiplexer #(.width(16)) multiplexer_8 (
    .in0(R_o2_q), .in1({VAR_i_despl, rf2}), .out(multiplexer_8_out), .sel(senales_de_control[4]));
  // Probe on estado
  or or_1 (clk, step_once, and_1_out);
  ROM #(.addrWidth(5), .dataWidth(25)) CU_ROM (
    .addr(estado),
    .data({VE, CSal, sES, ESnc, MCS, MOE, MWR, sDirM, LD_IR1, LD_IR2, LD_BR, sDatM, senales_de_control[7], LD_o1, LD_o2, senales_de_control[4], LD_ual, LD_PC, LD_PCi, sD}));
  // Probe on Cod_UAL
  LED led_44 ();  // open: in
  // Probe on ESnc
  // Probe on ual_1_y
  UAL ual_1 (.A(R_o1_q), .B(multiplexer_8_out), .ALU_OP(Cod_UAL), .Y(ual_1_y), .Z(Z));  // open: N, P
  Register #(.width(16)) R_ual (.D(ual_1_y), .en(LD_ual), .clk(clk), .Q(VAR_plus_rf));  // open: clr
  // Probe on {MCS, MOE, MWR, sDirM, LD_IR1, LD_IR2, LD_BR, sDatM, senales_de_control[7], LD_o1, LD_o2, senales_de_control[4], LD_ual, LD_PC, LD_PCi, sD}
  // Probe on VAR_plus_rf

  // Other names for the same wires on the sheet: senales_de_control (some bits) = {MCS, MOE, MWR, sDirM, LD_IR1, LD_IR2, LD_BR, sDatM, LD_o1, LD_o2, LD_ual, LD_PC, LD_PCi, sD};
  //   sI = senales_de_control[4]; sf2 = senales_de_control[7]; clk_enable = Clk_auto_tick_enabled;
  //   VAR_i_despl[4:0] = rf2

  // Notes on the sheet:
  //   PCi_STOP_addr: initial=0xffff
  //   Clk_auto_tick_enabled: initial=0x1
  //   3
  //   4
  //   5
  //   op/mov
  //   6
  //   7
  //   8
  //   Instrucción actual
  //   VAR_i_despl
  //   opi/movi
  //   9
  //   opi rd, rf1, #inmediato
  //   ldx, rd, VAR[rf1]
  //   stx, rf2, VAR[rf1]
  //   op rd, rf1, rf2
  //   movi rd, #inmediato
  //   ld rd, VAR
  //   st rf2, VAR
  //   mov rd, rf1
  //   beq rf1, ETIQUETA
  //   PC
  //   VAR_plus_rf1
  //   ld
  //   6
  //   6
  //   6
  //   6
  //   6
  //   0
  //   1
  //   2
  //   st
  //   10
  //   11
  //   5
  //   5
  //   5
  //   5
  //   5
  //   ldx
  //   12
  //   13
  //   14
  //   5
  //   5
  //   5
  //   5
  //   5
  //   Algoritmo de control ASM
  //   stx
  //   15
  //   16
  //   17
  //   18
  //   19
  //   1
  //   20
  //   16
  //   11
  //   16
  //   16
  //   16
  //   beq
  //   0
  //   5
  //   En principio, la señal Memory Chip Select sobra en este simulador
  //   ya que la memoria de Logisim-Evolution no la requiere.
  //   Buffer
  //   tri-estado
  //   Procesador BIRD
  //   Última modificación: 2025-12-18
  //   VAR_i_despl
  //   VAR_plus_rf1
  //   MUX EM
  //   Debugging controls
  //   rf2
  //   rd/rf2
  //   MUX i2
  //   contents of tabla_saltos (hex, n*v repeats v):
  //   9 0 c a 0 f 0 3 6 3 6 3 6 3 6 3 6 0 0 3 6 3 6 3 6 0 12
  //   (establece la direccion de progama (PCi) en la que se desea detener la simulación)
  //   rf1
  //   rd
  //   Código de opreración
  //   DESC
  //   (esta parte del procesador aparece simplificado en el esquema de clase)
  //   contents of ROM_UAL (hex, n*v repeats v):
  //   7*0 4 5 0 0 1 1 2 2 3 3 0 0 9 9 8 8 a a 0 4
  //   Unidad de Control
  //   VAR_i_despl
  //   MUX UAL
  //   Código UAL
  //   contents of CU_ROM (hex, n*v repeats v):
  //   1018806 1018404 1c00000 1000060 1000008 1800200 1000040 1000018 1800200 181a300 10000a0 1816000
  //   1000040 1000018 1819300 10000e0 1000018 1815000 1000040 0 1800005
  //   1) Editar bytecode (contenido de la memoria) en un archivo de texto
  //   2) Cargar el bytecode en la memoria (right-click sobre la memoria > "Load image")
  //   3) Establecer en PCi_STOP_addr la dirección de parada (la dir. de la última instrucción)
  //   4) Resetear PC a cero o reiniciar la simulación entera
  //   5) Iniciar simulación mediante auto-tick (Ctrl+K) o manualmente (botón "Step_once")
  //   estado siguiente / señales de control
  //   Instrucciones
  //   VAR_plus_rf1
  //   Estado siguiente (de código)
  //   no consecutivo
  //   Seleccionar Estado Siguiente
  //   Condicion de salto
  //   Variable de entrada que se 
  //    procesa en el estado
endmodule

module UAL (
  input  [15:0] A,
  input  [15:0] B,
  input  [3:0] ALU_OP,
  output [15:0] Y,
  output Z,
  output N,
  output P
);

  wire [15:0] add, add_1, bitwise_and, bitwise_or, bitwise_xor, div, mul, shift_left, shift_right, sub, sub_1;

  Adder #(.width(16)) adder_1 (.a(A), .b(B), .out(add));  // open: cin, cout
  Subtractor #(.width(16)) subtractor_1 (.a(A), .b(B), .out(sub));  // open: bin, bout
  Multiplier #(.width(16)) multiplier_1 (.a(A), .b(B), .out(mul));  // open: cin, cout
  Divider #(.width(16)) divider_1 (.a(A), .b(B), .out(div));  // open: upper, rem
  Adder #(.width(16)) adder_2 (.a(A), .b(B), .out(add_1));  // open: cin, cout
  Subtractor #(.width(16)) subtractor_2 (.a(A), .b(B), .out(sub_1));  // open: bin, bout
  assign bitwise_or = A | B;  // OR_Gate or_1, 16 bits wide
  assign bitwise_and = A & B;  // AND_Gate and_1, 16 bits wide
  assign bitwise_xor = A ^ B;  // XOR_Gate xor_1, 16 bits wide
  Shifter #(.width(16)) shifter_1 (.in(A), .\dist (B[3:0]), .out(shift_left));
  Shifter #(.shift("lr"), .width(16)) shifter_2 (.in(A), .\dist (B[3:0]), .out(shift_right));
  Multiplexer #(.select(4), .width(16)) multiplexer_1 (
    .in0(add), .in1(sub), .in2(mul), .in3(div), .in4(A), .in5(B), .in6(add_1), .in7(sub_1), .in8(bitwise_or),
    .in9(bitwise_and), .in10(bitwise_xor), .in11(shift_left), .in12(shift_right), .out(Y), .sel(ALU_OP));  // open: in13, in14, in15
  Comparator #(.width(16)) comparator_1 (.a(Y), .b({16{1'b0}}), .gt(P), .eq(Z), .lt(N));

  // Other names for the same wires on the sheet: shift_distance[3:0] = B[3:0]

  // Notes on the sheet:
  //   Unidad Aritmético Lógica del procesador BIRD
endmodule

// BR
module Banco_de_Registros (
  input  LD_BR,
  input  [15:0] DAT,
  input  [4:0] rf2,
  input  [4:0] rf1,
  input  [4:0] rd,
  input  clk,
  output [15:0] Q1,
  output [15:0] Q2
);

  wire LD_R0, LD_R1, LD_R2, LD_R3, LD_R4, LD_R5, LD_R6, LD_R7, LD_R8, LD_R9, LD_R10, LD_R11, LD_R12, LD_R13,
       LD_R14, LD_R15, LD_R16, LD_R17, LD_R18, LD_R19, LD_R20, LD_R21, LD_R22, LD_R23, LD_R24, LD_R25,
       LD_R26, LD_R27, LD_R28, LD_R29, LD_R30, LD_R31, OE1_R0, OE1_R1, OE1_R2, OE1_R3, OE1_R4, OE1_R5,
       OE1_R6, OE1_R7, OE1_R8, OE1_R9, OE1_R10, OE1_R11, OE1_R12, OE1_R13, OE1_R14, OE1_R15, OE1_R16,
       OE1_R17, OE1_R18, OE1_R19, OE1_R20, OE1_R21, OE1_R22, OE1_R23, OE1_R24, OE1_R25, OE1_R26, OE1_R27,
       OE1_R28, OE1_R29, OE1_R30, OE1_R31, OE2_R0, OE2_R1, OE2_R2, OE2_R3, OE2_R4, OE2_R5, OE2_R6, OE2_R7,
       OE2_R8, OE2_R9, OE2_R10, OE2_R11, OE2_R12, OE2_R13, OE2_R14, OE2_R15, OE2_R16, OE2_R17, OE2_R18,
       OE2_R19, OE2_R20, OE2_R21, OE2_R22, OE2_R23, OE2_R24, OE2_R25, OE2_R26, OE2_R27, OE2_R28, OE2_R29,
       OE2_R30, OE2_R31;
  wire [15:0] R1_q, R2_q, R3_q, R4_q, R5_q, R6_q, R7_q, R8_q, R9_q, R10_q, R11_q, R12_q, R13_q, R14_q, R15_q,
       R16_q, R17_q, R18_q, R19_q, R20_q, R21_q, R22_q, R23_q, R24_q, R25_q, R26_q, R27_q, R28_q, R29_q,
       R30_q, R31_q;

  Decoder #(.select(5)) decoder_1 (
    .out0(LD_R0), .out1(LD_R1), .out2(LD_R2), .out3(LD_R3), .out4(LD_R4), .out5(LD_R5), .out6(LD_R6),
    .out7(LD_R7), .out8(LD_R8), .out9(LD_R9), .out10(LD_R10), .out11(LD_R11), .out12(LD_R12), .out13(LD_R13),
    .out14(LD_R14), .out15(LD_R15), .out16(LD_R16), .out17(LD_R17), .out18(LD_R18), .out19(LD_R19),
    .out20(LD_R20), .out21(LD_R21), .out22(LD_R22), .out23(LD_R23), .out24(LD_R24), .out25(LD_R25),
    .out26(LD_R26), .out27(LD_R27), .out28(LD_R28), .out29(LD_R29), .out30(LD_R30), .out31(LD_R31), .sel(rd),
    .en(LD_BR));
  Decoder #(.enable("false"), .select(5)) decoder_2 (
    .out0(OE1_R0), .out1(OE1_R1), .out2(OE1_R2), .out3(OE1_R3), .out4(OE1_R4), .out5(OE1_R5), .out6(OE1_R6),
    .out7(OE1_R7), .out8(OE1_R8), .out9(OE1_R9), .out10(OE1_R10), .out11(OE1_R11), .out12(OE1_R12),
    .out13(OE1_R13), .out14(OE1_R14), .out15(OE1_R15), .out16(OE1_R16), .out17(OE1_R17), .out18(OE1_R18),
    .out19(OE1_R19), .out20(OE1_R20), .out21(OE1_R21), .out22(OE1_R22), .out23(OE1_R23), .out24(OE1_R24),
    .out25(OE1_R25), .out26(OE1_R26), .out27(OE1_R27), .out28(OE1_R28), .out29(OE1_R29), .out30(OE1_R30),
    .out31(OE1_R31), .sel(rf1));
  Decoder #(.enable("false"), .select(5)) decoder_3 (
    .out0(OE2_R0), .out1(OE2_R1), .out2(OE2_R2), .out3(OE2_R3), .out4(OE2_R4), .out5(OE2_R5), .out6(OE2_R6),
    .out7(OE2_R7), .out8(OE2_R8), .out9(OE2_R9), .out10(OE2_R10), .out11(OE2_R11), .out12(OE2_R12),
    .out13(OE2_R13), .out14(OE2_R14), .out15(OE2_R15), .out16(OE2_R16), .out17(OE2_R17), .out18(OE2_R18),
    .out19(OE2_R19), .out20(OE2_R20), .out21(OE2_R21), .out22(OE2_R22), .out23(OE2_R23), .out24(OE2_R24),
    .out25(OE2_R25), .out26(OE2_R26), .out27(OE2_R27), .out28(OE2_R28), .out29(OE2_R29), .out30(OE2_R30),
    .out31(OE2_R31), .sel(rf2));
  Register #(.width(16)) R4 (.D(DAT), .en(LD_R4), .clk(clk), .Q(R4_q));  // open: clr
  Register #(.width(16)) R8 (.D(DAT), .en(LD_R8), .clk(clk), .Q(R8_q));  // open: clr
  Register #(.width(16)) R12 (.D(DAT), .en(LD_R12), .clk(clk), .Q(R12_q));  // open: clr
  Register #(.width(16)) R16 (.D(DAT), .en(LD_R16), .clk(clk), .Q(R16_q));  // open: clr
  Register #(.width(16)) R20 (.D(DAT), .en(LD_R20), .clk(clk), .Q(R20_q));  // open: clr
  Register #(.width(16)) R24 (.D(DAT), .en(LD_R24), .clk(clk), .Q(R24_q));  // open: clr
  Register #(.width(16)) R28 (.D(DAT), .en(LD_R28), .clk(clk), .Q(R28_q));  // open: clr
  assign Q1 = OE1_R0 ? {16{1'b0}} : 16'bz;  // Controlled_Buffer controlled_buffer_1
  assign Q2 = OE2_R0 ? {16{1'b0}} : 16'bz;  // Controlled_Buffer controlled_buffer_2
  assign Q1 = OE1_R4 ? R4_q : 16'bz;  // Controlled_Buffer controlled_buffer_3
  assign Q2 = OE2_R4 ? R4_q : 16'bz;  // Controlled_Buffer controlled_buffer_4
  assign Q1 = OE1_R8 ? R8_q : 16'bz;  // Controlled_Buffer controlled_buffer_5
  assign Q2 = OE2_R8 ? R8_q : 16'bz;  // Controlled_Buffer controlled_buffer_6
  assign Q1 = OE1_R12 ? R12_q : 16'bz;  // Controlled_Buffer controlled_buffer_7
  assign Q2 = OE2_R12 ? R12_q : 16'bz;  // Controlled_Buffer controlled_buffer_8
  assign Q1 = OE1_R16 ? R16_q : 16'bz;  // Controlled_Buffer controlled_buffer_9
  assign Q2 = OE2_R16 ? R16_q : 16'bz;  // Controlled_Buffer controlled_buffer_10
  assign Q1 = OE1_R20 ? R20_q : 16'bz;  // Controlled_Buffer controlled_buffer_11
  assign Q2 = OE2_R20 ? R20_q : 16'bz;  // Controlled_Buffer controlled_buffer_12
  assign Q1 = OE1_R24 ? R24_q : 16'bz;  // Controlled_Buffer controlled_buffer_13
  assign Q2 = OE2_R24 ? R24_q : 16'bz;  // Controlled_Buffer controlled_buffer_14
  assign Q1 = OE1_R28 ? R28_q : 16'bz;  // Controlled_Buffer controlled_buffer_15
  assign Q2 = OE2_R28 ? R28_q : 16'bz;  // Controlled_Buffer controlled_buffer_16
  Register #(.width(16)) R1 (.D(DAT), .en(LD_R1), .clk(clk), .Q(R1_q));  // open: clr
  Register #(.width(16)) R5 (.D(DAT), .en(LD_R5), .clk(clk), .Q(R5_q));  // open: clr
  Register #(.width(16)) R9 (.D(DAT), .en(LD_R9), .clk(clk), .Q(R9_q));  // open: clr
  Register #(.width(16)) R13 (.D(DAT), .en(LD_R13), .clk(clk), .Q(R13_q));  // open: clr
  Register #(.width(16)) R17 (.D(DAT), .en(LD_R17), .clk(clk), .Q(R17_q));  // open: clr
  Register #(.width(16)) R21 (.D(DAT), .en(LD_R21), .clk(clk), .Q(R21_q));  // open: clr
  Register #(.width(16)) R25 (.D(DAT), .en(LD_R25), .clk(clk), .Q(R25_q));  // open: clr
  Register #(.width(16)) R29 (.D(DAT), .en(LD_R29), .clk(clk), .Q(R29_q));  // open: clr
  assign Q1 = OE1_R1 ? R1_q : 16'bz;  // Controlled_Buffer controlled_buffer_17
  assign Q2 = OE2_R1 ? R1_q : 16'bz;  // Controlled_Buffer controlled_buffer_18
  assign Q1 = OE1_R5 ? R5_q : 16'bz;  // Controlled_Buffer controlled_buffer_19
  assign Q2 = OE2_R5 ? R5_q : 16'bz;  // Controlled_Buffer controlled_buffer_20
  assign Q1 = OE1_R9 ? R9_q : 16'bz;  // Controlled_Buffer controlled_buffer_21
  assign Q2 = OE2_R9 ? R9_q : 16'bz;  // Controlled_Buffer controlled_buffer_22
  assign Q1 = OE1_R13 ? R13_q : 16'bz;  // Controlled_Buffer controlled_buffer_23
  assign Q2 = OE2_R13 ? R13_q : 16'bz;  // Controlled_Buffer controlled_buffer_24
  assign Q1 = OE1_R17 ? R17_q : 16'bz;  // Controlled_Buffer controlled_buffer_25
  assign Q2 = OE2_R17 ? R17_q : 16'bz;  // Controlled_Buffer controlled_buffer_26
  assign Q1 = OE1_R21 ? R21_q : 16'bz;  // Controlled_Buffer controlled_buffer_27
  assign Q2 = OE2_R21 ? R21_q : 16'bz;  // Controlled_Buffer controlled_buffer_28
  assign Q1 = OE1_R25 ? R25_q : 16'bz;  // Controlled_Buffer controlled_buffer_29
  assign Q2 = OE2_R25 ? R25_q : 16'bz;  // Controlled_Buffer controlled_buffer_30
  assign Q1 = OE1_R29 ? R29_q : 16'bz;  // Controlled_Buffer controlled_buffer_31
  assign Q2 = OE2_R29 ? R29_q : 16'bz;  // Controlled_Buffer controlled_buffer_32
  Register #(.width(16)) R2 (.D(DAT), .en(LD_R2), .clk(clk), .Q(R2_q));  // open: clr
  Register #(.width(16)) R6 (.D(DAT), .en(LD_R6), .clk(clk), .Q(R6_q));  // open: clr
  Register #(.width(16)) R10 (.D(DAT), .en(LD_R10), .clk(clk), .Q(R10_q));  // open: clr
  Register #(.width(16)) R14 (.D(DAT), .en(LD_R14), .clk(clk), .Q(R14_q));  // open: clr
  Register #(.width(16)) R18 (.D(DAT), .en(LD_R18), .clk(clk), .Q(R18_q));  // open: clr
  Register #(.width(16)) R22 (.D(DAT), .en(LD_R22), .clk(clk), .Q(R22_q));  // open: clr
  Register #(.width(16)) R26 (.D(DAT), .en(LD_R26), .clk(clk), .Q(R26_q));  // open: clr
  Register #(.width(16)) R30 (.D(DAT), .en(LD_R30), .clk(clk), .Q(R30_q));  // open: clr
  assign Q1 = OE1_R2 ? R2_q : 16'bz;  // Controlled_Buffer controlled_buffer_33
  assign Q2 = OE2_R2 ? R2_q : 16'bz;  // Controlled_Buffer controlled_buffer_34
  assign Q1 = OE1_R6 ? R6_q : 16'bz;  // Controlled_Buffer controlled_buffer_35
  assign Q2 = OE2_R6 ? R6_q : 16'bz;  // Controlled_Buffer controlled_buffer_36
  assign Q1 = OE1_R10 ? R10_q : 16'bz;  // Controlled_Buffer controlled_buffer_37
  assign Q2 = OE2_R10 ? R10_q : 16'bz;  // Controlled_Buffer controlled_buffer_38
  assign Q1 = OE1_R14 ? R14_q : 16'bz;  // Controlled_Buffer controlled_buffer_39
  assign Q2 = OE2_R14 ? R14_q : 16'bz;  // Controlled_Buffer controlled_buffer_40
  assign Q1 = OE1_R18 ? R18_q : 16'bz;  // Controlled_Buffer controlled_buffer_41
  assign Q2 = OE2_R18 ? R18_q : 16'bz;  // Controlled_Buffer controlled_buffer_42
  assign Q1 = OE1_R22 ? R22_q : 16'bz;  // Controlled_Buffer controlled_buffer_43
  assign Q2 = OE2_R22 ? R22_q : 16'bz;  // Controlled_Buffer controlled_buffer_44
  assign Q1 = OE1_R26 ? R26_q : 16'bz;  // Controlled_Buffer controlled_buffer_45
  assign Q2 = OE2_R26 ? R26_q : 16'bz;  // Controlled_Buffer controlled_buffer_46
  assign Q1 = OE1_R30 ? R30_q : 16'bz;  // Controlled_Buffer controlled_buffer_47
  assign Q2 = OE2_R30 ? R30_q : 16'bz;  // Controlled_Buffer controlled_buffer_48
  Register #(.width(16)) R3 (.D(DAT), .en(LD_R3), .clk(clk), .Q(R3_q));  // open: clr
  Register #(.width(16)) R7 (.D(DAT), .en(LD_R7), .clk(clk), .Q(R7_q));  // open: clr
  Register #(.width(16)) R11 (.D(DAT), .en(LD_R11), .clk(clk), .Q(R11_q));  // open: clr
  Register #(.width(16)) R15 (.D(DAT), .en(LD_R15), .clk(clk), .Q(R15_q));  // open: clr
  Register #(.width(16)) R19 (.D(DAT), .en(LD_R19), .clk(clk), .Q(R19_q));  // open: clr
  Register #(.width(16)) R23 (.D(DAT), .en(LD_R23), .clk(clk), .Q(R23_q));  // open: clr
  Register #(.width(16)) R27 (.D(DAT), .en(LD_R27), .clk(clk), .Q(R27_q));  // open: clr
  Register #(.width(16)) R31 (.D(DAT), .en(LD_R31), .clk(clk), .Q(R31_q));  // open: clr
  assign Q1 = OE1_R3 ? R3_q : 16'bz;  // Controlled_Buffer controlled_buffer_49
  assign Q2 = OE2_R3 ? R3_q : 16'bz;  // Controlled_Buffer controlled_buffer_50
  assign Q1 = OE1_R7 ? R7_q : 16'bz;  // Controlled_Buffer controlled_buffer_51
  assign Q2 = OE2_R7 ? R7_q : 16'bz;  // Controlled_Buffer controlled_buffer_52
  assign Q1 = OE1_R11 ? R11_q : 16'bz;  // Controlled_Buffer controlled_buffer_53
  assign Q2 = OE2_R11 ? R11_q : 16'bz;  // Controlled_Buffer controlled_buffer_54
  assign Q1 = OE1_R15 ? R15_q : 16'bz;  // Controlled_Buffer controlled_buffer_55
  assign Q2 = OE2_R15 ? R15_q : 16'bz;  // Controlled_Buffer controlled_buffer_56
  assign Q1 = OE1_R19 ? R19_q : 16'bz;  // Controlled_Buffer controlled_buffer_57
  assign Q2 = OE2_R19 ? R19_q : 16'bz;  // Controlled_Buffer controlled_buffer_58
  assign Q1 = OE1_R23 ? R23_q : 16'bz;  // Controlled_Buffer controlled_buffer_59
  assign Q2 = OE2_R23 ? R23_q : 16'bz;  // Controlled_Buffer controlled_buffer_60
  assign Q1 = OE1_R27 ? R27_q : 16'bz;  // Controlled_Buffer controlled_buffer_61
  assign Q2 = OE2_R27 ? R27_q : 16'bz;  // Controlled_Buffer controlled_buffer_62
  assign Q1 = OE1_R31 ? R31_q : 16'bz;  // Controlled_Buffer controlled_buffer_63
  assign Q2 = OE2_R31 ? R31_q : 16'bz;  // Controlled_Buffer controlled_buffer_64

  // Other names for the same wires on the sheet: LD_RB = LD_BR; ri1[4:0] = rf1; ri2[4:0] = rf2

  // Notes on the sheet:
  //   Banco de registros del procesador BIRD
  //   R0
endmodule
