// Logisim project BIRD_euskara.circ as structural Verilog: 4 circuits, main circuit PU
module PU (
);

  wire A_BEQ, A_LDX, A_OP, A_OPI, A_STX, add, addi, and_1_out, and_bis, andi, B, beq, bge, bgt, BIL1, BIL2,
       ble, bls, bne, call, clk, clock_1_out, comparator_1_eq, comparator_1_gt, decoder_1_out21,
       decoder_1_out22, decoder_1_out23, decoder_1_out24, decoder_1_out25, decoder_1_out26, decoder_1_out27,
       decoder_1_out28, decoder_1_out29, decoder_1_out30, decoder_1_out31, decoder_3_out10, decoder_3_out11,
       decoder_3_out12, decoder_3_out13, decoder_3_out14, decoder_3_out15, decoder_3_out16, decoder_3_out17,
       decoder_3_out18, decoder_3_out19, decoder_3_out20, decoder_3_out21, decoder_3_out22, decoder_3_out23,
       decoder_3_out24, decoder_3_out25, decoder_3_out26, decoder_3_out27, decoder_3_out28, decoder_3_out29,
       decoder_3_out30, decoder_3_out31, DESK, div, divi, hB, hD, hH, hMD, Id_OP, Id_OPI, Id_PC, in_bis,
       Ir_BEQ, Ir_LDX, Ir_OP, Ir_OPI, Ir_ST, Ir_STX, Jarraitu_out, jmp, JT, ld, ldd, ldx, M_Id_LD, M_Id_LDX,
       M_ST, M_STX, mov, mova, movi, mul, muli, multiplexer_6_out, not_1_out, not_2_out, not_3_out, or_1_out,
       or_bis, ori, out_bis, outm, outrm, outs, pop, push, ret, retm, SA, shl, shr, st, std, stx, sub, subi,
       xnor_1_out, xor_bis, xori, Z;
  wire [1:0] hMH;
  wire [3:0] UAL_kod;
  wire [4:0] egoera, Jauzi_Taula_data, JE, multiplexer_5_out, multiplexer_7_out, rh_ri2, ri1;
  wire [5:0] EK;
  wire [15:0] adder_1_out, ALD_B_despl, ALD_gehi_ri, EM_q1, EM_q2, mem_data_in, mem_data_out,
       multiplexer_1_out, multiplexer_2_out, multiplexer_3_out, multiplexer_4_out, multiplexer_8_out, PC,
       PCi, R_e1_q, ual_1_y;
  wire [16:1] Kontrol_seinaleak;

  LED led_1 (.in(ld));
  LED led_2 (.in(st));
  LED led_3 (.in(mov));
  LED led_4 (.in(add));
  LED led_5 (.in(sub));
  LED led_6 (.in(mul));
  LED led_7 (.in(div));
  LED led_8 (.in(and_bis));
  LED led_9 (.in(or_bis));
  LED led_10 (.in(xor_bis));
  Multiplexer #(.width(16)) multiplexer_1 (.in0(PC), .in1(PCi), .out(multiplexer_1_out), .sel(hD));
  Multiplexer #(.width(16)) multiplexer_2 (.in0(16'h1), .in1(ALD_B_despl), .out(multiplexer_2_out), .sel(hD));
  LED led_11 (.in(Ir_OP));
  LED led_12 (.in(A_OP));
  LED led_13 (.in(Id_OP));
  // Probe on EK
  LED led_14 (.in(ldx));
  LED led_15 (.in(stx));
  LED led_16 (.in(movi));
  LED led_17 (.in(addi));
  LED led_18 (.in(subi));
  LED led_19 (.in(muli));
  LED led_20 (.in(divi));
  LED led_21 (.in(andi));
  LED led_22 (.in(ori));
  LED led_23 (.in(xori));
  LED led_24 (.in(beq));
  Adder #(.width(16)) adder_1 (.a(multiplexer_1_out), .b(multiplexer_2_out), .out(adder_1_out));  // open: cin, cout
  // Probe on ALD_B_despl
  LED led_25 (.in(Ir_OPI));
  LED led_26 (.in(A_OPI));
  LED led_27 (.in(Id_OPI));
  Decoder #(.enable("false"), .select(5)) decoder_1 (
    .out0(BIL1), .out1(BIL2), .out2(DESK), .out3(Ir_OP), .out4(A_OP), .out5(Id_OP), .out6(Ir_OPI),
    .out7(A_OPI), .out8(Id_OPI), .out9(M_Id_LD), .out10(Ir_ST), .out11(M_ST), .out12(Ir_LDX), .out13(A_LDX),
    .out14(M_Id_LDX), .out15(Ir_STX), .out16(A_STX), .out17(M_STX), .out18(Ir_BEQ), .out19(A_BEQ),
    .out20(Id_PC), .out21(decoder_1_out21), .out22(decoder_1_out22), .out23(decoder_1_out23),
    .out24(decoder_1_out24), .out25(decoder_1_out25), .out26(decoder_1_out26), .out27(decoder_1_out27),
    .out28(decoder_1_out28), .out29(decoder_1_out29), .out30(decoder_1_out30), .out31(decoder_1_out31),
    .sel(egoera));
  Register #(.width(16)) u_PC (.D(adder_1_out), .en(Kontrol_seinaleak[2]), .clk(clk), .Q(PC));  // open: clr
  // Probe on adder_1_out
  LED led_28 (.in(M_Id_LD));
  // Probe on EK
  // Probe on EK
  // Probe on EK
  // Probe on EK
  // Probe on EK
  // Probe on PC
  // Probe on ALD_gehi_ri
  LED led_29 (.in(BIL1));
  LED led_30 (.in(BIL2));
  LED led_31 (.in(DESK));
  // Probe on EK
  LED led_32 (.in(Ir_ST));
  LED led_33 (.in(M_ST));
  // Probe on rh_ri2
  // Probe on rh_ri2
  // Probe on rh_ri2
  // Probe on rh_ri2
  Register #(.width(16)) u_PCi (.D(PC), .en(Kontrol_seinaleak[1]), .clk(clk), .Q(PCi));  // open: clr
  Multiplexer #(.select(2), .width(16)) multiplexer_3 (
    .in0(PC), .in1(ALD_gehi_ri), .in2(ALD_B_despl), .out(multiplexer_3_out), .sel(hMH));  // open: in3
  LED led_34 (.in(Ir_LDX));
  LED led_35 (.in(A_LDX));
  LED led_36 (.in(M_Id_LDX));
  // Probe on ri1
  // Probe on ri1
  // Probe on ri1
  // Probe on ri1
  RAM #(.addrWidth(16), .asyncread("true"), .dataWidth(16), .\type ("nonvolatile")) MEM (
    .addr(multiplexer_3_out), .we(Kontrol_seinaleak[14]), .oe(Kontrol_seinaleak[15]), .clk(clk),
    .din(mem_data_in), .dout(mem_data_out));
  // Probe on multiplexer_3_out
  // Probe on mem_data_in
  LED led_37 (.in(Ir_STX));
  LED led_38 (.in(A_STX));
  LED led_39 (.in(M_STX));
  // Probe on ALD_B_despl[15:8]
  // Probe on ALD_B_despl[15:8]
  // Probe on ALD_B_despl[15:8]
  LED led_40 (.in(Ir_BEQ));
  LED led_41 (.in(A_BEQ));
  LED led_42 (.in(Z));
  LED led_43 (.in(Id_PC));
  // Probe on ALD_B_despl[7:0]
  // Probe on ALD_B_despl[4:0]
  // Probe on ALD_B_despl[7:0]
  // Probe on ALD_B_despl[7:0]
  // Probe on mem_data_out
  Register #(.width(16)) IR1 (
    .D(mem_data_out), .en(Kontrol_seinaleak[11]), .clk(clk), .Q({EK, rh_ri2, ri1}));  // open: clr
  Register #(.width(16)) IR2 (.D(mem_data_out), .en(Kontrol_seinaleak[10]), .clk(clk), .Q(ALD_B_despl));  // open: clr
  Comparator #(.width(16)) comparator_1 (.a(PCi), .b(16'h14), .gt(comparator_1_gt), .eq(comparator_1_eq));  // open: lt
  // Probe on ri1
  // Probe on rh_ri2
  // Probe on EK
  // Probe on ALD_B_despl
  Clock clock_1 (.out(clock_1_out));
  or or_1 (or_1_out, comparator_1_gt, comparator_1_eq);
  not not_1 (not_1_out, or_1_out);
  // Probe on ALD_gehi_ri
  // Probe on ALD_B_despl[4:0]
  and and_1 (and_1_out, clock_1_out, not_1_out);
  Button Jarraitu (.out(Jarraitu_out));
  Multiplexer #(.width(16)) multiplexer_4 (.in0(ALD_gehi_ri), .in1(mem_data_out), .out(multiplexer_4_out), .sel(hMD));
  not not_2 (not_2_out, EK[5]);
  Decoder #(.select(5)) decoder_2 (
    .out0(ld), .out1(ldd), .out2(ldx), .out3(st), .out4(std), .out5(stx), .out6(mova), .out7(mov),
    .out8(movi), .out9(add), .out10(addi), .out11(sub), .out12(subi), .out13(mul), .out14(muli), .out15(div),
    .out16(divi), .out17(shr), .out18(shl), .out19(and_bis), .out20(andi), .out21(or_bis), .out22(ori),
    .out23(xor_bis), .out24(xori), .out25(jmp), .out26(beq), .out27(bne), .out28(bls), .out29(ble),
    .out30(bgt), .out31(bge), .sel(EK[4:0]), .en(not_2_out));
  Decoder #(.select(5)) decoder_3 (
    .out0(retm), .out1(call), .out2(ret), .out3(push), .out4(pop), .out5(in_bis), .out6(out_bis),
    .out7(outs), .out8(outm), .out9(outrm), .out10(decoder_3_out10), .out11(decoder_3_out11),
    .out12(decoder_3_out12), .out13(decoder_3_out13), .out14(decoder_3_out14), .out15(decoder_3_out15),
    .out16(decoder_3_out16), .out17(decoder_3_out17), .out18(decoder_3_out18), .out19(decoder_3_out19),
    .out20(decoder_3_out20), .out21(decoder_3_out21), .out22(decoder_3_out22), .out23(decoder_3_out23),
    .out24(decoder_3_out24), .out25(decoder_3_out25), .out26(decoder_3_out26), .out27(decoder_3_out27),
    .out28(decoder_3_out28), .out29(decoder_3_out29), .out30(decoder_3_out30), .out31(decoder_3_out31),
    .sel(EK[4:0]), .en(EK[5]));
  or or_2 (clk, and_1_out, Jarraitu_out);
  Multiplexer #(.width(5)) multiplexer_5 (.in0(ALD_B_despl[4:0]), .in1(rh_ri2), .out(multiplexer_5_out), .sel(hH));
  ROM #(.addrWidth(6), .dataWidth(4)) ROM_UAL (.addr(EK), .data(UAL_kod));
  ROM #(.addrWidth(6), .dataWidth(5)) Jauzi_Taula (.addr(EK), .data(Jauzi_Taula_data));
  // Probe on EK
  Multiplexer multiplexer_6 (.in0(Z), .in1(1'b1), .out(multiplexer_6_out), .sel(SA));
  // Probe on EM_q1
  Erregistro_Multzoa EM (
    .LD_RB(Kontrol_seinaleak[9]), .DAT(multiplexer_4_out), .ri2(multiplexer_5_out), .ri1(ri1), .rd(rh_ri2),
    .clk(clk), .Q1(EM_q1), .Q2(EM_q2));
  // Probe on EM_q2
  xnor xnor_1 (xnor_1_out, multiplexer_6_out, B);
  Register #(.width(16)) R_e1 (.D(EM_q1), .en(Kontrol_seinaleak[6]), .clk(clk), .Q(R_e1_q));  // open: clr
  Register #(.width(16)) R_e2 (.D(EM_q2), .en(Kontrol_seinaleak[5]), .clk(clk), .Q(mem_data_in));  // open: clr
  // Probe on UAL_kod
  Counter #(.max('h1f), .width(5)) STATE (
    .load(xnor_1_out), .up(1'b1), .count(not_3_out), .clk(clk), .D(multiplexer_7_out), .Q(egoera));  // open: clr, carry
  not not_3 (not_3_out, xnor_1_out);
  Multiplexer #(.width(5)) multiplexer_7 (.in0(JE), .in1(Jauzi_Taula_data), .out(multiplexer_7_out), .sel(JT));
  Multiplexer #(.width(16)) multiplexer_8 (.in0(mem_data_in), .in1(ALD_B_despl), .out(multiplexer_8_out), .sel(hB));
  // Probe on UAL_kod
  // Probe on egoera
  ROM #(.addrWidth(5), .dataWidth(25)) CU_ROM (
    .addr(egoera),
    .data({SA, B, JT, JE, Kontrol_seinaleak[16:14], hMH, Kontrol_seinaleak[11:9], hMD, hH, Kontrol_seinaleak[6:5], hB, Kontrol_seinaleak[3:1], hD}));
  UAL ual_1 (.A(R_e1_q), .B(multiplexer_8_out), .ALU_OP(UAL_kod), .Y(ual_1_y), .Z(Z));  // open: N, P
  Register #(.width(16)) R_ual (.D(ual_1_y), .en(Kontrol_seinaleak[3]), .clk(clk), .Q(ALD_gehi_ri));  // open: clr
  // Probe on ual_1_y
  // Probe on JE
  // Probe on ALD_gehi_ri
  // Probe on {Kontrol_seinaleak[16:14], hMH, Kontrol_seinaleak[11:9], hMD, hH, Kontrol_seinaleak[6:5], hB, Kontrol_seinaleak[3:1], hD}

  // Other names for the same wires on the sheet: Kontrol_seinaleak (some bits) = {hMH, hMD, hH, hB, hD};
  //   LD_PCi = Kontrol_seinaleak[1]; LD_PC = Kontrol_seinaleak[2]; LD_ual = Kontrol_seinaleak[3];
  //   LD_e2 = Kontrol_seinaleak[5]; LD_e1 = Kontrol_seinaleak[6]; LD_EM = Kontrol_seinaleak[9];
  //   LD_IR2 = Kontrol_seinaleak[10]; LD_IR1 = Kontrol_seinaleak[11]; MWR = Kontrol_seinaleak[14];
  //   MOE = Kontrol_seinaleak[15]; MCS = Kontrol_seinaleak[16]; ri2[4:0] = ALD_B_despl[4:0]

  // Notes on the sheet:
  //   3
  //   4
  //   5
  //   op/mov
  //   6
  //   7
  //   8
  //   opi/movi
  //   9
  //   opi rh, ri1, #bereh
  //   ldx, rh, ALD[ri1]
  //   stx, ri2, ALD[ri1]
  //   op rh, ri1, ri2
  //   movi rh, #bereh
  //   ld rh, ALD
  //   st ri2, ALD
  //   mov rh, ri1
  //   beq ri1, ETIKETA
  //   ld
  //   6
  //   6
  //   6
  //   6
  //   6
  //   BIRD prozesadorearen ASM kontrol-algoritmoa
  //   0
  //   1
  //   2
  //   st
  //   10
  //   11
  //   5
  //   5
  //   5
  //   5
  //   5
  //   ldx
  //   12
  //   13
  //   14
  //   5
  //   5
  //   5
  //   5
  //   5
  //   stx
  //   15
  //   16
  //   17
  //   11
  //   11
  //   18
  //   19
  //   1
  //   20
  //   16
  //   5
  //   16
  //   16
  //   beq
  //   0
  //   BIRD Konputagailua
  //   Exekuzioa eskuz debugeatzeko kontrola
  //   Gelditu exekuzioa PCi-k balio hau jasotzean
  //   Memory Chip Select seinalea soberan dago simuladore honetan,
  //   Logisim-Evolution-en memoriak ez duelako seinale honen beharrik
  //   MUX EM
  //   MUX i2
  //   contents of ROM_UAL (hex, n*v repeats v):
  //   7*0 4 5 0 0 1 1 2 2 3 3 0 0 9 9 8 8 a a 0 4
  //   contents of Jauzi_Taula (hex, n*v repeats v):
  //   9 0 c a 0 f 0 3 6 3 6 3 6 3 6 3 6 0 0 3 6 3 6 3 6 0 12
  //   MUX UAL
  //   contents of CU_ROM (hex, n*v repeats v):
  //   1018806 1018404 1c00000 1000060 1000008 1800200 1000040 1000018 1800200 181a300 10000a0 1816000
  //   1000040 1000018 1819300 10000e0 1000018 1815000 1000040 0 1800005
  //   BIRD prozesadorearen kontrol-unitate mikroprogramatua
  //   JE: Jauzia egiten bada, zein den hurr. egoera
  //   B: sarrera-aldagaiak hartu behar duen
  //   balioa kontrol-algoritmoan jauzia egiteko
  //   SA: prozesatu behar den sarrera aldagaia
endmodule

module CU_microprogrammed (
  input  [5:0] OP_CODE,
  input  Z,
  input  clk,
  output [16:0] control_signals
);

  wire B, JT, multiplexer_1_out, not_1_out, SA, xnor_1_out;
  wire [4:0] Jauzi_Taula_data, JE, multiplexer_2_out, state;

  ROM #(.addrWidth(5), .dataWidth(25)) CU_ROM (.addr(state), .data({SA, B, JT, JE, control_signals}));
  // Probe on state
  // Probe on control_signals
  // Probe on JE
  ROM #(.addrWidth(6), .dataWidth(5)) Jauzi_Taula (.addr(OP_CODE), .data(Jauzi_Taula_data));
  Multiplexer multiplexer_1 (.in0(Z), .in1(1'b1), .out(multiplexer_1_out), .sel(SA));
  xnor xnor_1 (xnor_1_out, multiplexer_1_out, B);
  Multiplexer #(.width(5)) multiplexer_2 (.in0(JE), .in1(Jauzi_Taula_data), .out(multiplexer_2_out), .sel(JT));
  Counter #(.max('h1f), .width(5)) u_STATE (
    .load(xnor_1_out), .up(1'b1), .count(not_1_out), .clk(clk), .D(multiplexer_2_out), .Q(state));  // open: clr, carry
  not not_1 (not_1_out, xnor_1_out);

  // Other names for the same wires on the sheet: hD = control_signals[0]; LD_PCi = control_signals[1];
  //   LD_PC = control_signals[2]; LD_ual = control_signals[3]; hB = control_signals[4]; LD_e2 = control_signals[5];
  //   LD_e1 = control_signals[6]; hH = control_signals[7]; hMD = control_signals[8]; LD_EM = control_signals[9];
  //   LD_IR2 = control_signals[10]; LD_IR1 = control_signals[11]; hMH[1:0] = control_signals[13:12];
  //   MWR = control_signals[14]; MOE = control_signals[15]; MCS = control_signals[16]

  // Notes on the sheet:
  //   contents of CU_ROM (hex, n*v repeats v):
  //   1018806 1018404 1c00000 1000060 1000008 1800200 1000040 1000018 1800200 181a300 10000a0 1816000
  //   1000040 1000018 1819300 10000e0 1000018 1815000 1000040 0 1800005
  //   contents of Jauzi_Taula (hex, n*v repeats v):
  //   9 0 c a 0 f 0 3 6 3 6 3 6 3 6 3 6 0 0 3 6 3 6 3 6 0 12
endmodule

module UAL (
  input  [15:0] A,
  input  [15:0] B,
  input  [3:0] ALU_OP,
  output [15:0] Y,
  output Z,
  output N,
  output P
);

  wire [15:0] add, add_1, bitwise_and, bitwise_or, bitwise_xor, div, mul, shift_left, shift_right, sub, sub_1;

  Adder #(.width(16)) adder_1 (.a(A), .b(B), .out(add));  // open: cin, cout
  Subtractor #(.width(16)) subtractor_1 (.a(A), .b(B), .out(sub));  // open: bin, bout
  Multiplier #(.width(16)) multiplier_1 (.a(A), .b(B), .out(mul));  // open: cin, cout
  Divider #(.width(16)) divider_1 (.a(A), .b(B), .out(div));  // open: upper, rem
  Adder #(.width(16)) adder_2 (.a(A), .b(B), .out(add_1));  // open: cin, cout
  Subtractor #(.width(16)) subtractor_2 (.a(A), .b(B), .out(sub_1));  // open: bin, bout
  assign bitwise_or = A | B;  // OR_Gate or_1, 16 bits wide
  assign bitwise_and = A & B;  // AND_Gate and_1, 16 bits wide
  assign bitwise_xor = A ^ B;  // XOR_Gate xor_1, 16 bits wide
  Shifter #(.width(16)) shifter_1 (.in(A), .\dist (B[3:0]), .out(shift_left));
  Shifter #(.shift("lr"), .width(16)) shifter_2 (.in(A), .\dist (B[3:0]), .out(shift_right));
  Multiplexer #(.select(4), .width(16)) multiplexer_1 (
    .in0(add), .in1(sub), .in2(mul), .in3(div), .in4(A), .in5(B), .in6(add_1), .in7(sub_1), .in8(bitwise_or),
    .in9(bitwise_and), .in10(bitwise_xor), .in11(shift_left), .in12(shift_right), .out(Y), .sel(ALU_OP));  // open: in13, in14, in15
  Comparator #(.width(16)) comparator_1 (.a(Y), .b({16{1'b0}}), .gt(P), .eq(Z), .lt(N));

  // Other names for the same wires on the sheet: shift_distance[3:0] = B[3:0]
endmodule

// EM
module Erregistro_Multzoa (
  input  LD_RB,
  input  [15:0] DAT,
  input  [4:0] ri2,
  input  [4:0] ri1,
  input  [4:0] rd,
  input  clk,
  output [15:0] Q1,
  output [15:0] Q2
);

  wire LD_R0, LD_R1, LD_R2, LD_R3, LD_R4, LD_R5, LD_R6, LD_R7, LD_R8, LD_R9, LD_R10, LD_R11, LD_R12, LD_R13,
       LD_R14, LD_R15, LD_R16, LD_R17, LD_R18, LD_R19, LD_R20, LD_R21, LD_R22, LD_R23, LD_R24, LD_R25,
       LD_R26, LD_R27, LD_R28, LD_R29, LD_R30, LD_R31, OE1_R0, OE1_R1, OE1_R2, OE1_R3, OE1_R4, OE1_R5,
       OE1_R6, OE1_R7, OE1_R8, OE1_R9, OE1_R10, OE1_R11, OE1_R12, OE1_R13, OE1_R14, OE1_R15, OE1_R16,
       OE1_R17, OE1_R18, OE1_R19, OE1_R20, OE1_R21, OE1_R22, OE1_R23, OE1_R24, OE1_R25, OE1_R26, OE1_R27,
       OE1_R28, OE1_R29, OE1_R30, OE1_R31, OE2_R0, OE2_R1, OE2_R2, OE2_R3, OE2_R4, OE2_R5, OE2_R6, OE2_R7,
       OE2_R8, OE2_R9, OE2_R10, OE2_R11, OE2_R12, OE2_R13, OE2_R14, OE2_R15, OE2_R16, OE2_R17, OE2_R18,
       OE2_R19, OE2_R20, OE2_R21, OE2_R22, OE2_R23, OE2_R24, OE2_R25, OE2_R26, OE2_R27, OE2_R28, OE2_R29,
       OE2_R30, OE2_R31;
  wire [15:0] R1_q, R2_q, R3_q, R4_q, R5_q, R6_q, R7_q, R8_q, R9_q, R10_q, R11_q, R12_q, R13_q, R14_q, R15_q,
       R16_q, R17_q, R18_q, R19_q, R20_q, R21_q, R22_q, R23_q, R24_q, R25_q, R26_q, R27_q, R28_q, R29_q,
       R30_q, R31_q;

  Decoder #(.select(5)) decoder_1 (
    .out0(LD_R0), .out1(LD_R1), .out2(LD_R2), .out3(LD_R3), .out4(LD_R4), .out5(LD_R5), .out6(LD_R6),
    .out7(LD_R7), .out8(LD_R8), .out9(LD_R9), .out10(LD_R10), .out11(LD_R11), .out12(LD_R12), .out13(LD_R13),
    .out14(LD_R14), .out15(LD_R15), .out16(LD_R16), .out17(LD_R17), .out18(LD_R18), .out19(LD_R19),
    .out20(LD_R20), .out21(LD_R21), .out22(LD_R22), .out23(LD_R23), .out24(LD_R24), .out25(LD_R25),
    .out26(LD_R26), .out27(LD_R27), .out28(LD_R28), .out29(LD_R29), .out30(LD_R30), .out31(LD_R31), .sel(rd),
    .en(LD_RB));
  Decoder #(.enable("false"), .select(5)) decoder_2 (
    .out0(OE1_R0), .out1(OE1_R1), .out2(OE1_R2), .out3(OE1_R3), .out4(OE1_R4), .out5(OE1_R5), .out6(OE1_R6),
    .out7(OE1_R7), .out8(OE1_R8), .out9(OE1_R9), .out10(OE1_R10), .out11(OE1_R11), .out12(OE1_R12),
    .out13(OE1_R13), .out14(OE1_R14), .out15(OE1_R15), .out16(OE1_R16), .out17(OE1_R17), .out18(OE1_R18),
    .out19(OE1_R19), .out20(OE1_R20), .out21(OE1_R21), .out22(OE1_R22), .out23(OE1_R23), .out24(OE1_R24),
    .out25(OE1_R25), .out26(OE1_R26), .out27(OE1_R27), .out28(OE1_R28), .out29(OE1_R29), .out30(OE1_R30),
    .out31(OE1_R31), .sel(ri1));
  Decoder #(.enable("false"), .select(5)) decoder_3 (
    .out0(OE2_R0), .out1(OE2_R1), .out2(OE2_R2), .out3(OE2_R3), .out4(OE2_R4), .out5(OE2_R5), .out6(OE2_R6),
    .out7(OE2_R7), .out8(OE2_R8), .out9(OE2_R9), .out10(OE2_R10), .out11(OE2_R11), .out12(OE2_R12),
    .out13(OE2_R13), .out14(OE2_R14), .out15(OE2_R15), .out16(OE2_R16), .out17(OE2_R17), .out18(OE2_R18),
    .out19(OE2_R19), .out20(OE2_R20), .out21(OE2_R21), .out22(OE2_R22), .out23(OE2_R23), .out24(OE2_R24),
    .out25(OE2_R25), .out26(OE2_R26), .out27(OE2_R27), .out28(OE2_R28), .out29(OE2_R29), .out30(OE2_R30),
    .out31(OE2_R31), .sel(ri2));
  Register #(.width(16)) R4 (.D(DAT), .en(LD_R4), .clk(clk), .Q(R4_q));  // open: clr
  Register #(.width(16)) R8 (.D(DAT), .en(LD_R8), .clk(clk), .Q(R8_q));  // open: clr
  Register #(.width(16)) R12 (.D(DAT), .en(LD_R12), .clk(clk), .Q(R12_q));  // open: clr
  Register #(.width(16)) R16 (.D(DAT), .en(LD_R16), .clk(clk), .Q(R16_q));  // open: clr
  Register #(.width(16)) R20 (.D(DAT), .en(LD_R20), .clk(clk), .Q(R20_q));  // open: clr
  Register #(.width(16)) R24 (.D(DAT), .en(LD_R24), .clk(clk), .Q(R24_q));  // open: clr
  Register #(.width(16)) R28 (.D(DAT), .en(LD_R28), .clk(clk), .Q(R28_q));  // open: clr
  assign Q1 = OE1_R0 ? {16{1'b0}} : 16'bz;  // Controlled_Buffer controlled_buffer_1
  assign Q2 = OE2_R0 ? {16{1'b0}} : 16'bz;  // Controlled_Buffer controlled_buffer_2
  assign Q1 = OE1_R4 ? R4_q : 16'bz;  // Controlled_Buffer controlled_buffer_3
  assign Q2 = OE2_R4 ? R4_q : 16'bz;  // Controlled_Buffer controlled_buffer_4
  assign Q1 = OE1_R8 ? R8_q : 16'bz;  // Controlled_Buffer controlled_buffer_5
  assign Q2 = OE2_R8 ? R8_q : 16'bz;  // Controlled_Buffer controlled_buffer_6
  assign Q1 = OE1_R12 ? R12_q : 16'bz;  // Controlled_Buffer controlled_buffer_7
  assign Q2 = OE2_R12 ? R12_q : 16'bz;  // Controlled_Buffer controlled_buffer_8
  assign Q1 = OE1_R16 ? R16_q : 16'bz;  // Controlled_Buffer controlled_buffer_9
  assign Q2 = OE2_R16 ? R16_q : 16'bz;  // Controlled_Buffer controlled_buffer_10
  assign Q1 = OE1_R20 ? R20_q : 16'bz;  // Controlled_Buffer controlled_buffer_11
  assign Q2 = OE2_R20 ? R20_q : 16'bz;  // Controlled_Buffer controlled_buffer_12
  assign Q1 = OE1_R24 ? R24_q : 16'bz;  // Controlled_Buffer controlled_buffer_13
  assign Q2 = OE2_R24 ? R24_q : 16'bz;  // Controlled_Buffer controlled_buffer_14
  assign Q1 = OE1_R28 ? R28_q : 16'bz;  // Controlled_Buffer controlled_buffer_15
  assign Q2 = OE2_R28 ? R28_q : 16'bz;  // Controlled_Buffer controlled_buffer_16
  Register #(.width(16)) R1 (.D(DAT), .en(LD_R1), .clk(clk), .Q(R1_q));  // open: clr
  Register #(.width(16)) R5 (.D(DAT), .en(LD_R5), .clk(clk), .Q(R5_q));  // open: clr
  Register #(.width(16)) R9 (.D(DAT), .en(LD_R9), .clk(clk), .Q(R9_q));  // open: clr
  Register #(.width(16)) R13 (.D(DAT), .en(LD_R13), .clk(clk), .Q(R13_q));  // open: clr
  Register #(.width(16)) R17 (.D(DAT), .en(LD_R17), .clk(clk), .Q(R17_q));  // open: clr
  Register #(.width(16)) R21 (.D(DAT), .en(LD_R21), .clk(clk), .Q(R21_q));  // open: clr
  Register #(.width(16)) R25 (.D(DAT), .en(LD_R25), .clk(clk), .Q(R25_q));  // open: clr
  Register #(.width(16)) R29 (.D(DAT), .en(LD_R29), .clk(clk), .Q(R29_q));  // open: clr
  assign Q1 = OE1_R1 ? R1_q : 16'bz;  // Controlled_Buffer controlled_buffer_17
  assign Q2 = OE2_R1 ? R1_q : 16'bz;  // Controlled_Buffer controlled_buffer_18
  assign Q1 = OE1_R5 ? R5_q : 16'bz;  // Controlled_Buffer controlled_buffer_19
  assign Q2 = OE2_R5 ? R5_q : 16'bz;  // Controlled_Buffer controlled_buffer_20
  assign Q1 = OE1_R9 ? R9_q : 16'bz;  // Controlled_Buffer controlled_buffer_21
  assign Q2 = OE2_R9 ? R9_q : 16'bz;  // Controlled_Buffer controlled_buffer_22
  assign Q1 = OE1_R13 ? R13_q : 16'bz;  // Controlled_Buffer controlled_buffer_23
  assign Q2 = OE2_R13 ? R13_q : 16'bz;  // Controlled_Buffer controlled_buffer_24
  assign Q1 = OE1_R17 ? R17_q : 16'bz;  // Controlled_Buffer controlled_buffer_25
  assign Q2 = OE2_R17 ? R17_q : 16'bz;  // Controlled_Buffer controlled_buffer_26
  assign Q1 = OE1_R21 ? R21_q : 16'bz;  // Controlled_Buffer controlled_buffer_27
  assign Q2 = OE2_R21 ? R21_q : 16'bz;  // Controlled_Buffer controlled_buffer_28
  assign Q1 = OE1_R25 ? R25_q : 16'bz;  // Controlled_Buffer controlled_buffer_29
  assign Q2 = OE2_R25 ? R25_q : 16'bz;  // Controlled_Buffer controlled_buffer_30
  assign Q1 = OE1_R29 ? R29_q : 16'bz;  // Controlled_Buffer controlled_buffer_31
  assign Q2 = OE2_R29 ? R29_q : 16'bz;  // Controlled_Buffer controlled_buffer_32
  Register #(.width(16)) R2 (.D(DAT), .en(LD_R2), .clk(clk), .Q(R2_q));  // open: clr
  Register #(.width(16)) R6 (.D(DAT), .en(LD_R6), .clk(clk), .Q(R6_q));  // open: clr
  Register #(.width(16)) R10 (.D(DAT), .en(LD_R10), .clk(clk), .Q(R10_q));  // open: clr
  Register #(.width(16)) R14 (.D(DAT), .en(LD_R14), .clk(clk), .Q(R14_q));  // open: clr
  Register #(.width(16)) R18 (.D(DAT), .en(LD_R18), .clk(clk), .Q(R18_q));  // open: clr
  Register #(.width(16)) R22 (.D(DAT), .en(LD_R22), .clk(clk), .Q(R22_q));  // open: clr
  Register #(.width(16)) R26 (.D(DAT), .en(LD_R26), .clk(clk), .Q(R26_q));  // open: clr
  Register #(.width(16)) R30 (.D(DAT), .en(LD_R30), .clk(clk), .Q(R30_q));  // open: clr
  assign Q1 = OE1_R2 ? R2_q : 16'bz;  // Controlled_Buffer controlled_buffer_33
  assign Q2 = OE2_R2 ? R2_q : 16'bz;  // Controlled_Buffer controlled_buffer_34
  assign Q1 = OE1_R6 ? R6_q : 16'bz;  // Controlled_Buffer controlled_buffer_35
  assign Q2 = OE2_R6 ? R6_q : 16'bz;  // Controlled_Buffer controlled_buffer_36
  assign Q1 = OE1_R10 ? R10_q : 16'bz;  // Controlled_Buffer controlled_buffer_37
  assign Q2 = OE2_R10 ? R10_q : 16'bz;  // Controlled_Buffer controlled_buffer_38
  assign Q1 = OE1_R14 ? R14_q : 16'bz;  // Controlled_Buffer controlled_buffer_39
  assign Q2 = OE2_R14 ? R14_q : 16'bz;  // Controlled_Buffer controlled_buffer_40
  assign Q1 = OE1_R18 ? R18_q : 16'bz;  // Controlled_Buffer controlled_buffer_41
  assign Q2 = OE2_R18 ? R18_q : 16'bz;  // Controlled_Buffer controlled_buffer_42
  assign Q1 = OE1_R22 ? R22_q : 16'bz;  // Controlled_Buffer controlled_buffer_43
  assign Q2 = OE2_R22 ? R22_q : 16'bz;  // Controlled_Buffer controlled_buffer_44
  assign Q1 = OE1_R26 ? R26_q : 16'bz;  // Controlled_Buffer controlled_buffer_45
  assign Q2 = OE2_R26 ? R26_q : 16'bz;  // Controlled_Buffer controlled_buffer_46
  assign Q1 = OE1_R30 ? R30_q : 16'bz;  // Controlled_Buffer controlled_buffer_47
  assign Q2 = OE2_R30 ? R30_q : 16'bz;  // Controlled_Buffer controlled_buffer_48
  Register #(.width(16)) R3 (.D(DAT), .en(LD_R3), .clk(clk), .Q(R3_q));  // open: clr
  Register #(.width(16)) R7 (.D(DAT), .en(LD_R7), .clk(clk), .Q(R7_q));  // open: clr
  Register #(.width(16)) R11 (.D(DAT), .en(LD_R11), .clk(clk), .Q(R11_q));  // open: clr
  Register #(.width(16)) R15 (.D(DAT), .en(LD_R15), .clk(clk), .Q(R15_q));  // open: clr
  Register #(.width(16)) R19 (.D(DAT), .en(LD_R19), .clk(clk), .Q(R19_q));  // open: clr
  Register #(.width(16)) R23 (.D(DAT), .en(LD_R23), .clk(clk), .Q(R23_q));  // open: clr
  Register #(.width(16)) R27 (.D(DAT), .en(LD_R27), .clk(clk), .Q(R27_q));  // open: clr
  Register #(.width(16)) R31 (.D(DAT), .en(LD_R31), .clk(clk), .Q(R31_q));  // open: clr
  assign Q1 = OE1_R3 ? R3_q : 16'bz;  // Controlled_Buffer controlled_buffer_49
  assign Q2 = OE2_R3 ? R3_q : 16'bz;  // Controlled_Buffer controlled_buffer_50
  assign Q1 = OE1_R7 ? R7_q : 16'bz;  // Controlled_Buffer controlled_buffer_51
  assign Q2 = OE2_R7 ? R7_q : 16'bz;  // Controlled_Buffer controlled_buffer_52
  assign Q1 = OE1_R11 ? R11_q : 16'bz;  // Controlled_Buffer controlled_buffer_53
  assign Q2 = OE2_R11 ? R11_q : 16'bz;  // Controlled_Buffer controlled_buffer_54
  assign Q1 = OE1_R15 ? R15_q : 16'bz;  // Controlled_Buffer controlled_buffer_55
  assign Q2 = OE2_R15 ? R15_q : 16'bz;  // Controlled_Buffer controlled_buffer_56
  assign Q1 = OE1_R19 ? R19_q : 16'bz;  // Controlled_Buffer controlled_buffer_57
  assign Q2 = OE2_R19 ? R19_q : 16'bz;  // Controlled_Buffer controlled_buffer_58
  assign Q1 = OE1_R23 ? R23_q : 16'bz;  // Controlled_Buffer controlled_buffer_59
  assign Q2 = OE2_R23 ? R23_q : 16'bz;  // Controlled_Buffer controlled_buffer_60
  assign Q1 = OE1_R27 ? R27_q : 16'bz;  // Controlled_Buffer controlled_buffer_61
  assign Q2 = OE2_R27 ? R27_q : 16'bz;  // Controlled_Buffer controlled_buffer_62
  assign Q1 = OE1_R31 ? R31_q : 16'bz;  // Controlled_Buffer controlled_buffer_63
  assign Q2 = OE2_R31 ? R31_q : 16'bz;  // Controlled_Buffer controlled_buffer_64

  // Notes on the sheet:
  //   R0
endmodule
